// Logisim project Single_cycle_block.circ as structural Verilog: 1 circuit, main circuit main
module main (
);

  wire [19:0] main_1_pc_output;
  wire [31:0] alu_1_alu_result, main_2_instruction, main_3_p1, main_3_p2;

  pc_new_main main_1 (.PC_Output(main_1_pc_output));  // open: Pc_Selctor, Imm16, RS1, Immu, ImmL
  Instruction_Mem_main main_2 (.Address(main_1_pc_output), .Instruction(main_2_instruction));
  // regfile_new_main main_3: pin names not known; wires that end beside it: main_3_p1, main_3_p2
  ALU alu_1 (
    .ALU_Result(alu_1_alu_result), .A(main_3_p1), .B(main_3_p2));  // open: less_flag_unsign, Overflow, less_flag, Zero_flag, ALU_Opration
  // Data_Mem_main main_4: pin names not known

  // Notes on the sheet:
  //   op_code
  //   function
endmodule
